// Digital circuit AND10.dig as structural Verilog
module AND10 (
  input  _1,
  input  _2,
  input  _3,
  input  _4,
  input  _5,
  input  _6,
  input  _7,
  input  _8,
  input  _9,
  input  _10,
  output Y
);

  wire and_1_out, and_2_out, and_3_out, and_4_out, and_5_out, and_6_out, and_7_out, and_8_out;

  and and_1 (and_1_out, _1, _2);
  and and_2 (and_2_out, _3, _4);
  and and_3 (and_3_out, _5, _6);
  and and_4 (and_4_out, _7, _8);
  and and_5 (and_5_out, _9, _10);
  and and_6 (and_6_out, and_1_out, and_2_out);
  and and_7 (and_7_out, and_4_out, and_5_out);
  and and_8 (and_8_out, and_3_out, and_7_out);
  and and_9 (Y, and_6_out, and_8_out);
endmodule
