// Digital circuit BinaryToDecimal.dig as structural Verilog
module BinaryToDecimal (
  input  A0,
  input  A1,
  input  A2,
  input  A3,
  input  A4,
  input  A5,
  input  A6,
  input  A7,
  output _7,
  output _6,
  output _5,
  output _4,
  output _3,
  output _2,
  output _1,
  output _0
);

  wire encoder_1_a, encoder_1_b, encoder_1_c;

  Encoder encoder_1 (
    .A0(A0), .A1(A1), .A2(A2), .A3(A3), .A4(A4), .A5(A5), .A6(A6), .A7(A7), .A(encoder_1_a), .B(encoder_1_b),
    .C(encoder_1_c));  // open: G1, NO, G
  Decoder decoder_1 (
    .C(encoder_1_c), .B(encoder_1_b), .A(encoder_1_a), ._7(_7), ._6(_6), ._5(_5), ._4(_4), ._3(_3), ._2(_2),
    ._1(_1), ._0(_0));
endmodule
