// Digital circuit Decoder.dig as structural Verilog
module Decoder (
  input  C,
  input  B,
  input  A,
  output _7,
  output _6,
  output _5,
  output _4,
  output _3,
  output _2,
  output _1,
  output _0
);

  wire not_1_out, not_2_out, not_3_out;

  not not_1 (not_1_out, C);
  not not_2 (not_2_out, B);
  not not_3 (not_3_out, A);
  and and_1 (_7, C, B, A);
  and and_2 (_6, not_1_out, B, A);
  and and_3 (_5, C, not_2_out, A);
  and and_4 (_4, not_1_out, not_2_out, A);
  and and_5 (_3, C, B, not_3_out);
  and and_6 (_2, not_1_out, B, not_3_out);
  and and_7 (_1, C, not_2_out, not_3_out);
  and and_8 (_0, not_3_out, not_2_out, not_1_out);
endmodule
