// Digital circuit Encoder.dig as structural Verilog
module Encoder (
  input  A0,
  input  A1,
  input  A2,
  input  A3,
  input  A4,
  input  A5,
  input  A6,
  input  A7,
  input  G1,
  output A,
  output B,
  output C,
  output NO,
  output G
);

  wire and_1_out, and_2_out, and_3_out, and_4_out, and_5_out, not_1_out, not_2_out, not_3_out, not_4_out,
       not_5_out, not_6_out, not_7_out, not_8_out;

  not not_1 (not_1_out, A0);
  not not_2 (not_2_out, A2);
  not not_3 (not_3_out, A4);
  not not_4 (not_4_out, A5);
  not not_5 (not_5_out, A6);
  and and_1 (and_1_out, not_4_out, not_3_out, A3);
  and and_2 (and_2_out, not_4_out, not_3_out, A2);
  and and_3 (and_3_out, not_5_out, A5);
  and and_4 (and_4_out, not_5_out, not_3_out, A3);
  and and_5 (and_5_out, not_5_out, not_3_out, not_2_out, A1);
  or or_1 (A, A4, A5, A6, A7);
  or or_2 (B, A7, A6, and_1_out, and_2_out);
  or or_3 (C, A7, and_3_out, and_4_out, and_5_out);
  not not_6 (not_6_out, A);
  not not_7 (not_7_out, B);
  not not_8 (not_8_out, C);
  and and_6 (NO, not_6_out, not_7_out, not_8_out, not_1_out);

  assign G = G1;

  // Notes on the sheet:
  //   Priority Encoder 8:3
endmodule
