// Digital circuit EncoderT.dig as structural Verilog
module EncoderT (
  input  A0,
  input  A1,
  input  A2,
  input  A3,
  input  A4,
  input  A5,
  input  A6,
  input  A7,
  input  EI,
  output A,
  output B,
  output C,
  output NO,
  output GS,
  output EO
);

  wire and_1_out, and_2_out, and_3_out, and_4_out, and_5_out, not_1_out, not_2_out, not_3_out, not_4_out,
       not_5_out, not_6_out, not_7_out, not_8_out, or_1_out, or_2_out, or_3_out;

  not not_1 (not_1_out, A0);
  not not_2 (not_2_out, A2);
  not not_3 (not_3_out, A4);
  not not_4 (not_4_out, A5);
  not not_5 (not_5_out, A6);
  or or_1 (or_1_out, A4, A5, A6, A7);
  and and_1 (and_1_out, EI, not_4_out, not_3_out, A3);
  and and_2 (and_2_out, EI, not_4_out, not_3_out, A2);
  and and_3 (and_3_out, not_5_out, EI, A5);
  and and_4 (and_4_out, EI, not_5_out, not_3_out, A3);
  and and_5 (and_5_out, not_5_out, not_3_out, EI, not_2_out, A1);
  and and_6 (A, EI, or_1_out);
  or or_2 (or_2_out, A7, A6, and_1_out, and_2_out);
  or or_3 (or_3_out, A7, and_3_out, and_4_out, and_5_out);
  // AND7 and7_1: pin names not known; wires that end beside it: A0, A1, A1, A2, A3, A4, A5, A6, A7, EI, EO
  and and_7 (B, EI, or_2_out);
  and and_8 (C, EI, or_3_out);
  and and_9 (GS, EO, EI);
  not not_6 (not_6_out, A);
  not not_7 (not_7_out, B);
  not not_8 (not_8_out, C);
  and and_10 (NO, not_6_out, not_7_out, not_8_out, not_1_out);

  // Notes on the sheet:
  //   Priority Encoder 8:3
endmodule
