// Digital circuit FSM-Esercizio27.dig as structural Verilog
module FSM_Esercizio27 (
  input  C,
  input  R,
  output Y
);

  wire and_1_out, and_2_out, and_3_out, and_4_out, and_5_out, and_6_out, not_1_out, not_2_out, not_3_out,
       not_4_out, not_5_out, not_6_out, not_7_out, not_8_out, or_1_out, or_2_out, or_3_out,
       registro3b_1_s0_2, registro3b_1_s1_2, registro3b_1_s2_2;

  not not_1 (not_1_out, registro3b_1_s0_2);
  not not_2 (not_2_out, registro3b_1_s0_2);
  not not_3 (not_3_out, registro3b_1_s2_2);
  not not_4 (not_4_out, registro3b_1_s2_2);
  not not_5 (not_5_out, registro3b_1_s1_2);
  and and_1 (and_1_out, registro3b_1_s2_2, registro3b_1_s0_2);
  and and_2 (and_2_out, registro3b_1_s1_2, not_1_out);
  and and_3 (and_3_out, registro3b_1_s1_2, not_2_out);
  and and_4 (and_4_out, not_3_out, registro3b_1_s0_2);
  and and_5 (and_5_out, not_4_out, not_5_out);
  and and_6 (and_6_out, registro3b_1_s2_2, registro3b_1_s1_2);
  or or_1 (or_1_out, and_1_out, and_2_out);
  or or_2 (or_2_out, and_3_out, and_4_out);
  or or_3 (or_3_out, and_5_out, and_6_out);
  Registro3B registro3b_1 (
    .S2(or_1_out), .S1(or_2_out), .S0(or_3_out), .S2_2(registro3b_1_s2_2), .S1_2(registro3b_1_s1_2),
    .S0_2(registro3b_1_s0_2), .C(C), .R(R));
  not not_6 (not_6_out, registro3b_1_s2_2);
  not not_7 (not_7_out, registro3b_1_s1_2);
  not not_8 (not_8_out, registro3b_1_s0_2);
  and and_7 (Y, not_6_out, not_7_out, not_8_out);
endmodule
