// Digital circuit FSM_Esercizio22.dig as structural Verilog
module FSM_Esercizio22 (
  input  A,
  input  B,
  input  CLK,
  input  R,
  output Q
);

  wire and_1_out, and_2_out, not_1_out, not_2_out, not_3_out, not_4_out, registro2b_1_s0_2, registro2b_1_s1_2;

  not not_1 (not_1_out, registro2b_1_s0_2);
  not not_2 (not_2_out, registro2b_1_s1_2);
  not not_3 (not_3_out, registro2b_1_s1_2);
  and and_1 (and_1_out, A, not_1_out, not_2_out);
  and and_2 (and_2_out, B, not_3_out, registro2b_1_s0_2);
  Registro2B registro2b_1 (
    .S0(and_1_out), .S1(and_2_out), .S0_2(registro2b_1_s0_2), .S1_2(registro2b_1_s1_2), .R(R), .C(CLK));
  not not_4 (not_4_out, registro2b_1_s0_2);
  and and_3 (Q, not_4_out, registro2b_1_s1_2);
endmodule
