// Digital circuit FSM_Esercizio26.dig as structural Verilog
module FSM_Esercizio26 (
  input  A,
  input  B
);

  wire and_1_out, and_2_out, not_1_out, not_2_out, not_3_out, or_1_out, registro3b_1_s0_2, registro3b_1_s1_2,
       registro3b_1_s2_2, xor_1_out, xor_2_out;

  xor xor_1 (xor_1_out, B, A, registro3b_1_s0_2);
  xor xor_2 (xor_2_out, A, registro3b_1_s2_2, registro3b_1_s1_2);
  and and_1 (and_1_out, not_1_out, registro3b_1_s1_2, xor_1_out);
  not not_1 (not_1_out, registro3b_1_s2_2);
  and and_2 (and_2_out, xor_2_out, not_2_out, not_3_out);
  not not_2 (not_2_out, registro3b_1_s0_2);
  not not_3 (not_3_out, B);
  or or_1 (or_1_out, and_1_out, and_2_out);
  Registro3B registro3b_1 (
    .S2(or_1_out), .S2_2(registro3b_1_s2_2), .S1_2(registro3b_1_s1_2), .S0_2(registro3b_1_s0_2));  // open: S1, S0, C, R
endmodule
