// Digital circuit FlipFlop-JK.dig as structural Verilog
module FlipFlop_JK (
  input  J,
  input  K,
  input  gt_C,
  output QC,
  output Q
);

  wire and_1_out, and_2_out, not_1_out, or_1_out;

  not not_1 (not_1_out, K);
  and and_1 (and_1_out, QC, J);
  and and_2 (and_2_out, not_1_out, Q);
  or or_1 (or_1_out, and_1_out, and_2_out);
  D_FF d_ff_1 (.D(or_1_out), .C(gt_C), .Q(Q), .nQ(QC));
endmodule
