// Digital circuit FlipFlop-R.dig as structural Verilog
module FlipFlop_R (
  input  D,
  input  Reset,
  input  Clock,
  output Q
);

  wire and_1_out, not_1_out;

  not not_1 (not_1_out, Reset);
  and and_1 (and_1_out, D, not_1_out);
  D_FF d_ff_1 (.D(and_1_out), .C(Clock), .Q(Q));  // open: nQ
endmodule
