// Digital circuit FlipFlop-Reset.dig as structural Verilog
module FlipFlop_Reset (
  input  D,
  input  R,
  input  C,
  output Q
);

  wire and_1_out, not_1_out;

  and and_1 (and_1_out, D, not_1_out);
  not not_1 (not_1_out, R);
  D_FF d_ff_1 (.D(and_1_out), .C(C), .Q(Q));  // open: nQ
endmodule
