// Digital circuit FlipFlopJK-to-FlipFlopD.dig as structural Verilog
module FlipFlopJK_to_FlipFlopD (
  input  D,
  input  C,
  output Q,
  output Q_2
);

  wire not_1_out;

  not not_1 (not_1_out, D);
  FlipFlop_JK flipflop_jk_1 (.Q(Q), .QC(Q_2), .gt_C(C), .J(D), .K(not_1_out));
endmodule
