// Digital circuit FlipFlopJK-to-FlipFlopT.dig as structural Verilog
module FlipFlopJK_to_FlipFlopT (
  input  T,
  input  C,
  output Q,
  output Q_2
);

  FlipFlop_JK flipflop_jk_1 (.Q(Q), .QC(Q_2), .gt_C(C), .J(T), .K(T));
endmodule
