// Digital circuit FullAdd.dig as structural Verilog
module FullAdd (
  input  A,
  input  B,
  input  RI,
  output S,
  output RO
);

  wire and_1_out, and_2_out, and_3_out;

  xor xor_1 (S, B, A, RI);
  and and_1 (and_1_out, B, A);
  and and_2 (and_2_out, B, RI);
  and and_3 (and_3_out, RI, A);
  or or_1 (RO, and_1_out, and_2_out, and_3_out);
endmodule
