// Digital circuit FullAddWave.dig as structural Verilog
module FullAddWave (
  input  [1:0] B,
  input  [1:0] A,
  input  in_6,
  output S1,
  output Ro,
  output S0
);

  wire fulladd_2_ro;

  FullAdd fulladd_1 (.A(A[1]), .B(B[1]), .RI(fulladd_2_ro), .S(S1), .RO(Ro));
  FullAdd fulladd_2 (.A(A[0]), .B(B[0]), .RI(in_6), .S(S0), .RO(fulladd_2_ro));
endmodule
