// Digital circuit FullAddWave4B.dig as structural Verilog
module FullAddWave4B (
  input  [3:0] B,
  input  [3:0] A,
  input  in_6,
  output R,
  output S1,
  output S0,
  output S2,
  output S3
);

  wire fulladdwave2b_2_ro;

  FullAddWave2B fulladdwave2b_1 (.Ro(R), .S1(S3), .S0(S2), .A(A[3:2]), .B(B[3:2]), .Ri(fulladdwave2b_2_ro));
  FullAddWave2B fulladdwave2b_2 (.Ro(fulladdwave2b_2_ro), .S1(S1), .S0(S0), .A(A[1:0]), .B(B[1:0]), .Ri(in_6));
endmodule
