// Digital circuit FullSub2B.dig as structural Verilog
module FullSub2B (
  input  [1:0] A,
  input  [1:0] B,
  output out_3,
  output out_4,
  output out_5
);

  wire [1:0] not_1_out;

  FullAddWave2B fulladdwave2b_1 (.Ro(out_5), .S1(out_4), .S0(out_3), .A(A), .B(not_1_out), .Ri(1'b1));
  assign not_1_out = ~B;  // Not not_1, 2 bits wide
endmodule
