// Digital circuit Multiplex4.dig as structural Verilog
module Multiplex4 (
  input  D0,
  input  D1,
  input  D2,
  input  D3,
  input  S0,
  input  S1,
  output Y
);

  wire and_1_out, and_2_out, and_3_out, and_4_out, not_1_out, not_2_out;

  not not_1 (not_1_out, S0);
  not not_2 (not_2_out, S1);
  and and_1 (and_1_out, D0, not_1_out, not_2_out);
  and and_2 (and_2_out, D1, not_1_out, S1);
  and and_3 (and_3_out, D2, S0, not_2_out);
  and and_4 (and_4_out, D3, S0, S1);
  or or_1 (Y, and_1_out, and_2_out, and_3_out, and_4_out);
endmodule
