// Digital circuit Multiplex8.dig as structural Verilog
module Multiplex8 (
  input  D0,
  input  D1,
  input  D2,
  input  D3,
  input  D4,
  input  D5,
  input  D6,
  input  D7,
  input  S1,
  input  S0,
  input  S2,
  output Y
);

  wire multiplexer_1_out, multiplexer_2_out, multiplexer_3_out, multiplexer_4_out, multiplexer_5_out,
       multiplexer_6_out;

  Multiplexer multiplexer_1 (.sel(S0), .in_0(D0), .in_1(D1), .out(multiplexer_1_out));
  Multiplexer multiplexer_2 (.sel(S0), .in_0(D2), .in_1(D3), .out(multiplexer_2_out));
  Multiplexer multiplexer_3 (.sel(S0), .in_0(D4), .in_1(D5), .out(multiplexer_3_out));
  Multiplexer multiplexer_4 (.sel(S0), .in_0(D6), .in_1(D7), .out(multiplexer_4_out));
  Multiplexer multiplexer_5 (.sel(S1), .in_0(multiplexer_1_out), .in_1(multiplexer_2_out), .out(multiplexer_5_out));
  Multiplexer multiplexer_6 (.sel(S1), .in_0(multiplexer_3_out), .in_1(multiplexer_4_out), .out(multiplexer_6_out));
  Multiplexer multiplexer_7 (.sel(S2), .in_0(multiplexer_5_out), .in_1(multiplexer_6_out), .out(Y));
endmodule
