// Digital circuit Registro2B.dig as structural Verilog
module Registro2B (
  input  S0,
  input  S1,
  input  R,
  input  C,
  output S0_2,
  output S1_2
);

  FlipFlop_Reset flipflop_reset_1 (.D(S0), .R(R), .C(C), .Q(S0_2));
  FlipFlop_Reset flipflop_reset_2 (.D(S1), .R(R), .C(C), .Q(S1_2));
endmodule
