// Digital circuit Registro3B.dig as structural Verilog
module Registro3B (
  input  S2,
  input  S1,
  input  S0,
  input  C,
  input  R,
  output S2_2,
  output S1_2,
  output S0_2
);

  FlipFlop_Reset flipflop_reset_1 (.D(S2), .R(R), .C(C), .Q(S2_2));
  FlipFlop_Reset flipflop_reset_2 (.D(S1), .R(R), .C(C), .Q(S1_2));
  FlipFlop_Reset flipflop_reset_3 (.D(S0), .R(R), .C(C), .Q(S0_2));
endmodule
