// Digital circuit RegistroStato.dig as structural Verilog
module RegistroStato (
  input  S0,
  input  S1,
  input  C,
  input  R,
  output S0_2,
  output S1_2
);

  FlipFlop_R flipflop_r_1 (.D(S0), .Reset(R), .Clock(C), .Q(S0_2));
  FlipFlop_R flipflop_r_2 (.D(S1), .Reset(R), .Clock(C), .Q(S1_2));
endmodule
